// Logisim project decoder.circ as structural Verilog: 1 circuit, main circuit main
module main (
  input  in_1,
  input  in_2,
  input  in_3,
  input  in_4,
  input  in_5,
  output out_6,
  output out_7,
  output out_8,
  output out_9,
  output out_10,
  output out_11
);

  wire and_5_out, and_8_out, and_9_out, and_10_out, and_11_out, and_12_out, not_1_out, not_2_out, not_3_out;

  not not_1 (not_1_out, in_1);
  not not_2 (not_2_out, in_3);
  and and_1 (out_6, in_1, in_3);
  and and_2 (out_7, in_1, not_2_out);
  and and_3 (out_9, not_1_out, in_3);
  and and_4 (out_11, not_1_out, not_2_out);
  not not_3 (not_3_out, in_2);
  not not_4 (not_3_out, in_4);
  not not_5 (not_3_out, in_4);
  and and_5 (and_5_out, not_3_out, not_3_out, not_3_out);
  and and_6 (out_8, not_3_out, in_2, in_4);
  and and_7 (out_10, not_3_out, not_3_out, in_4);
  and and_8 (and_8_out, not_3_out, not_3_out, in_4, in_4);
  and and_9 (and_9_out, not_3_out, not_3_out, in_4);
  and and_10 (and_10_out, not_3_out, not_3_out, not_3_out);
  and and_11 (and_11_out, not_3_out, not_3_out, in_4);
  and and_12 (and_12_out, not_3_out, not_3_out, not_3_out, not_3_out);

  assign in_5 = in_4;
endmodule
